// Logisim project NANDToCPU.circ as structural Verilog
module half_adder (
  input  in_1,
  input  in_2,
  output out_3,
  output out_4
);

  and and_1 (out_3, in_1, in_2);
  xor xor_1 (out_4, in_1, in_2);
endmodule

module Full_Adder (
  input  A,
  input  B,
  input  Carry,
  output C_Out,
  output Sum
);

  wire and_1_out, half_adder_1_out_3, half_adder_1_out_4;

  half_adder half_adder_1 (.in_1(B), .in_2(Carry), .out_3(half_adder_1_out_3), .out_4(half_adder_1_out_4));
  and and_1 (and_1_out, A, half_adder_1_out_4);
  xor xor_1 (Sum, A, half_adder_1_out_4);
  xor xor_2 (C_Out, and_1_out, half_adder_1_out_3);
endmodule

module _4_Bit_Adder (
  input  [3:0] in_1,
  input  [3:0] in_2,
  output out_3,
  output [3:0] out_4
);

  wire full_adder_1_c_out, full_adder_2_c_out, full_adder_3_c_out;

  Full_Adder full_adder_1 (.A(in_1[0]), .B(in_2[0]), .Carry(1'b0), .C_Out(full_adder_1_c_out), .Sum(out_4[0]));
  Full_Adder full_adder_2 (
    .A(in_1[1]), .B(in_2[1]), .Carry(full_adder_1_c_out), .C_Out(full_adder_2_c_out), .Sum(out_4[1]));
  Full_Adder full_adder_3 (
    .A(in_2[2]), .B(in_1[2]), .Carry(full_adder_2_c_out), .C_Out(full_adder_3_c_out), .Sum(out_4[2]));
  Full_Adder full_adder_4 (.A(in_2[3]), .B(in_1[3]), .Carry(full_adder_3_c_out), .C_Out(out_3), .Sum(out_4[3]));
endmodule

module _16_Bit_Adder__2 (
  input  in_1,
  input  [15:0] A,
  input  [15:0] B,
  output out_4,
  output [15:0] Sum
);

  wire full_adder_1_c_out, full_adder_2_c_out, full_adder_3_c_out, full_adder_4_c_out, full_adder_5_c_out,
       full_adder_6_c_out, full_adder_7_c_out, full_adder_8_c_out, full_adder_9_c_out, full_adder_10_c_out,
       full_adder_11_c_out, full_adder_12_c_out, full_adder_13_c_out, full_adder_14_c_out,
       full_adder_15_c_out;

  Full_Adder full_adder_1 (.A(A[0]), .B(B[0]), .Carry(in_1), .C_Out(full_adder_1_c_out), .Sum(Sum[0]));
  Full_Adder full_adder_2 (.A(A[1]), .B(B[1]), .Carry(full_adder_1_c_out), .C_Out(full_adder_2_c_out), .Sum(Sum[1]));
  Full_Adder full_adder_3 (.A(A[2]), .B(B[2]), .Carry(full_adder_2_c_out), .C_Out(full_adder_3_c_out), .Sum(Sum[2]));
  Full_Adder full_adder_4 (.A(A[3]), .B(B[3]), .Carry(full_adder_3_c_out), .C_Out(full_adder_4_c_out), .Sum(Sum[3]));
  Full_Adder full_adder_5 (.A(A[4]), .B(B[4]), .Carry(full_adder_4_c_out), .C_Out(full_adder_5_c_out), .Sum(Sum[4]));
  Full_Adder full_adder_6 (.A(A[5]), .B(B[5]), .Carry(full_adder_5_c_out), .C_Out(full_adder_6_c_out), .Sum(Sum[5]));
  Full_Adder full_adder_7 (.A(A[6]), .B(B[6]), .Carry(full_adder_6_c_out), .C_Out(full_adder_7_c_out), .Sum(Sum[6]));
  Full_Adder full_adder_8 (.A(A[7]), .B(B[7]), .Carry(full_adder_7_c_out), .C_Out(full_adder_8_c_out), .Sum(Sum[7]));
  Full_Adder full_adder_9 (.A(A[8]), .B(B[8]), .Carry(full_adder_8_c_out), .C_Out(full_adder_9_c_out), .Sum(Sum[8]));
  Full_Adder full_adder_10 (.A(A[9]), .B(B[9]), .Carry(full_adder_9_c_out), .C_Out(full_adder_10_c_out), .Sum(Sum[9]));
  Full_Adder full_adder_11 (
    .A(A[10]), .B(B[10]), .Carry(full_adder_10_c_out), .C_Out(full_adder_11_c_out), .Sum(Sum[10]));
  Full_Adder full_adder_12 (
    .A(A[11]), .B(B[11]), .Carry(full_adder_11_c_out), .C_Out(full_adder_12_c_out), .Sum(Sum[11]));
  Full_Adder full_adder_13 (
    .A(A[12]), .B(B[12]), .Carry(full_adder_12_c_out), .C_Out(full_adder_13_c_out), .Sum(Sum[12]));
  Full_Adder full_adder_14 (
    .A(A[13]), .B(B[13]), .Carry(full_adder_13_c_out), .C_Out(full_adder_14_c_out), .Sum(Sum[13]));
  Full_Adder full_adder_15 (
    .A(A[14]), .B(B[14]), .Carry(full_adder_14_c_out), .C_Out(full_adder_15_c_out), .Sum(Sum[14]));
  Full_Adder full_adder_16 (.A(A[15]), .B(B[15]), .Carry(full_adder_15_c_out), .C_Out(out_4), .Sum(Sum[15]));
endmodule

module Increment_16_Bit (
  input  [15:0] in_1,
  output [15:0] out_2,
  output out_3
);

  _16_Bit_Adder__2 u_16_bit_adder_2_1 (.Sum(out_2), .A(in_1), .B(16'h1), .out_4(out_3), .in_1(1'b0));
endmodule

module _16_Bit_Subtracter (
  input  [15:0] in_1,
  input  [15:0] in_2,
  output out_3,
  output [15:0] out_4
);

  wire increment_16_bit_1_out_3;
  wire [15:0] increment_16_bit_1_out_2, not_1_out;

  assign not_1_out = ~in_2;  // NOT_Gate not_1, 16 bits wide
  Increment_16_Bit increment_16_bit_1 (
    .in_1(not_1_out), .out_2(increment_16_bit_1_out_2), .out_3(increment_16_bit_1_out_3));
  _16_Bit_Adder__2 u_16_bit_adder_2_1 (
    .Sum(out_4), .A(in_1), .B(increment_16_bit_1_out_2), .out_4(out_3), .in_1(increment_16_bit_1_out_3));
endmodule

module _16_Bit_Equal_to_Zero (
  input  [15:0] in_1,
  output out_2
);

  wire or_1_out, or_2_out, or_3_out, or_4_out, or_5_out, or_6_out, or_7_out, or_8_out, or_9_out, or_10_out,
       or_11_out, or_12_out, or_13_out, or_14_out, or_15_out;

  or or_1 (or_1_out, in_1[0], in_1[1]);
  or or_2 (or_2_out, in_1[2], in_1[3]);
  or or_3 (or_3_out, in_1[4], in_1[5]);
  or or_4 (or_4_out, in_1[6], in_1[7]);
  or or_5 (or_5_out, in_1[8], in_1[9]);
  or or_6 (or_6_out, in_1[10], in_1[11]);
  or or_7 (or_7_out, in_1[12], in_1[13]);
  or or_8 (or_8_out, in_1[14], in_1[15]);
  or or_9 (or_9_out, or_1_out, or_2_out);
  or or_10 (or_10_out, or_3_out, or_4_out);
  or or_11 (or_11_out, or_5_out, or_6_out);
  or or_12 (or_12_out, or_7_out, or_8_out);
  or or_13 (or_13_out, or_9_out, or_10_out);
  or or_14 (or_14_out, or_11_out, or_12_out);
  not not_1 (out_2, or_15_out);
  or or_15 (or_15_out, or_13_out, or_14_out);
endmodule

module _16_Bit_Less_than_Zero (
  input  [15:0] in_1,
  output out_2
);


  assign out_2 = in_1[15];
endmodule

module Selector (
  input  Data_1,
  input  Data_0,
  input  Select,
  output Output
);

  wire and_1_out, and_2_out, not_1_out;

  not not_1 (not_1_out, Select);
  and and_1 (and_1_out, Data_1, Select);
  and and_2 (and_2_out, not_1_out, Data_0);
  or or_1 (Output, and_1_out, and_2_out);
endmodule

module Switch (
  input  Data,
  input  Select,
  output _1,
  output _0
);

  wire not_1_out;

  not not_1 (not_1_out, Select);
  and and_1 (_1, Data, Select);
  and and_2 (_0, Data, not_1_out);
endmodule

module Latch (
  input  Store,
  input  Data,
  output Output,
  output nOutput
);

  wire and_1_out, and_2_out, not_1_out;

  not not_1 (not_1_out, Data);
  and and_1 (and_1_out, not_1_out, Store);
  and and_2 (and_2_out, Store, Data);
  nor nor_1 (Output, and_1_out, nOutput);
  nor nor_2 (nOutput, Output, and_2_out);
endmodule

module Data_Flip_Flop (
  input  Store,
  input  Data,
  input  Clock,
  output out_4
);

  wire and_1_out, latch_1_output, not_1_out;

  not not_1 (not_1_out, Clock);
  and and_1 (and_1_out, Store, not_1_out);
  Latch latch_1 (.Store(and_1_out), .Data(Data), .Output(latch_1_output));  // open: nOutput
  Latch latch_2 (.Store(Clock), .Data(latch_1_output), .Output(out_4));  // open: nOutput
endmodule

module _2_Bit_Register (
  input  Data_1,
  input  Data_0,
  input  Store,
  output out_4,
  output out_5
);

  wire clock_1_out;

  Clock clock_1 (.out(clock_1_out));
  Data_Flip_Flop data_flip_flop_1 (.Store(Store), .Data(Data_1), .out_4(out_4), .Clock(clock_1_out));
  Data_Flip_Flop data_flip_flop_2 (.Store(Store), .Data(Data_0), .out_4(out_5), .Clock(clock_1_out));
endmodule

module _8_Bit_Register (
  input  [7:0] in_1,
  input  in_2,
  output [7:0] out_3
);

  wire clock_1_out;

  Clock clock_1 (.out(clock_1_out));
  Data_Flip_Flop data_flip_flop_1 (.Store(in_2), .Data(in_1[0]), .out_4(out_3[0]), .Clock(clock_1_out));
  Data_Flip_Flop data_flip_flop_2 (.Store(in_2), .Data(in_1[1]), .out_4(out_3[1]), .Clock(clock_1_out));
  Data_Flip_Flop data_flip_flop_3 (.Store(in_2), .Data(in_1[2]), .out_4(out_3[2]), .Clock(clock_1_out));
  Data_Flip_Flop data_flip_flop_4 (.Store(in_2), .Data(in_1[3]), .out_4(out_3[3]), .Clock(clock_1_out));
  Data_Flip_Flop data_flip_flop_5 (.Store(in_2), .Data(in_1[4]), .out_4(out_3[4]), .Clock(clock_1_out));
  Data_Flip_Flop data_flip_flop_6 (.Store(in_2), .Data(in_1[5]), .out_4(out_3[5]), .Clock(clock_1_out));
  Data_Flip_Flop data_flip_flop_7 (.Store(in_2), .Data(in_1[6]), .out_4(out_3[6]), .Clock(clock_1_out));
  Data_Flip_Flop data_flip_flop_8 (.Store(in_2), .Data(in_1[7]), .out_4(out_3[7]), .Clock(clock_1_out));
endmodule

module _16_Bit_Register (
  input  Store,
  input  Clock,
  input  [15:0] Input,
  output [15:0] Output
);

  Data_Flip_Flop data_flip_flop_1 (.Store(Store), .Data(Input[0]), .out_4(Output[0]), .Clock(Clock));
  Data_Flip_Flop data_flip_flop_2 (.Store(Store), .Data(Input[1]), .out_4(Output[1]), .Clock(Clock));
  Data_Flip_Flop data_flip_flop_3 (.Store(Store), .Data(Input[2]), .out_4(Output[2]), .Clock(Clock));
  Data_Flip_Flop data_flip_flop_4 (.Store(Store), .Data(Input[3]), .out_4(Output[3]), .Clock(Clock));
  Data_Flip_Flop data_flip_flop_5 (.Store(Store), .Data(Input[4]), .out_4(Output[4]), .Clock(Clock));
  Data_Flip_Flop data_flip_flop_6 (.Store(Store), .Data(Input[5]), .out_4(Output[5]), .Clock(Clock));
  Data_Flip_Flop data_flip_flop_7 (.Store(Store), .Data(Input[6]), .out_4(Output[6]), .Clock(Clock));
  Data_Flip_Flop data_flip_flop_8 (.Store(Store), .Data(Input[7]), .out_4(Output[7]), .Clock(Clock));
  Data_Flip_Flop data_flip_flop_9 (.Store(Store), .Data(Input[8]), .out_4(Output[8]), .Clock(Clock));
  Data_Flip_Flop data_flip_flop_10 (.Store(Store), .Data(Input[9]), .out_4(Output[9]), .Clock(Clock));
  Data_Flip_Flop data_flip_flop_11 (.Store(Store), .Data(Input[10]), .out_4(Output[10]), .Clock(Clock));
  Data_Flip_Flop data_flip_flop_12 (.Store(Store), .Data(Input[11]), .out_4(Output[11]), .Clock(Clock));
  Data_Flip_Flop data_flip_flop_13 (.Store(Store), .Data(Input[12]), .out_4(Output[12]), .Clock(Clock));
  Data_Flip_Flop data_flip_flop_14 (.Store(Store), .Data(Input[13]), .out_4(Output[13]), .Clock(Clock));
  Data_Flip_Flop data_flip_flop_15 (.Store(Store), .Data(Input[14]), .out_4(Output[14]), .Clock(Clock));
  Data_Flip_Flop data_flip_flop_16 (.Store(Store), .Data(Input[15]), .out_4(Output[15]), .Clock(Clock));
endmodule

module Counter (
  input  Clock,
  input  [15:0] Data,
  input  Store,
  output [15:0] Output
);

  wire not_1_out;
  wire [15:0] bitselector_1_out, increment_16_bit_1_out_2;

  Increment_16_Bit increment_16_bit_1 (.in_1(Output), .out_2(increment_16_bit_1_out_2));  // open: out_3
  BitSelector #(.width(32), .group(16)) bitselector_1 (
    .in({Data, increment_16_bit_1_out_2}), .out(bitselector_1_out), .sel(Store));
  not not_1 (not_1_out, Clock);
  _16_Bit_Register u_16_bit_register_1 (.Store(not_1_out), .Clock(Clock), .Input(bitselector_1_out), .Output(Output));
endmodule

module _2_Address_RAM (
  input  Store,
  input  [15:0] in_2,
  input  Address,
  input  Clock,
  output [15:0] out_5
);

  wire switch_1__0, switch_1__1;
  wire [15:0] n16_bit_register_1_output, n16_bit_register_2_output;

  Switch switch_1 (.Data(Store), .Select(Address), ._1(switch_1__1), ._0(switch_1__0));
  _16_Bit_Register u_16_bit_register_1 (
    .Store(switch_1__1), .Clock(Clock), .Input(in_2), .Output(n16_bit_register_1_output));
  _16_Bit_Register u_16_bit_register_2 (
    .Store(switch_1__0), .Clock(Clock), .Input(in_2), .Output(n16_bit_register_2_output));
  BitSelector #(.width(32), .group(16)) bitselector_1 (
    .in({n16_bit_register_1_output, n16_bit_register_2_output}), .out(out_5), .sel(Address));
endmodule

module Unary_ALU (
  input  [15:0] X,
  input  Z,
  input  N,
  output [15:0] Output
);

  wire [15:0] bitselector_1_out, not_1_out;

  BitSelector #(.width(32), .group(16)) bitselector_1 (.in({{16{1'b0}}, X}), .out(bitselector_1_out), .sel(Z));
  assign not_1_out = ~bitselector_1_out;  // NOT_Gate not_1, 16 bits wide
  BitSelector #(.width(32), .group(16)) bitselector_2 (.in({not_1_out, bitselector_1_out}), .out(Output), .sel(N));
endmodule

module Full_ALU (
  input  [15:0] X,
  input  [15:0] Y,
  input  ZX,
  input  NX,
  input  ZY,
  input  NY,
  input  F,
  input  NO,
  output [15:0] out_9
);

  wire [15:0] and_1_out, bitselector_1_out, n16_bit_adder_2_1_sum, not_1_out, unary_alu_1_output,
       unary_alu_2_output;

  Unary_ALU unary_alu_1 (.X(X), .Z(ZX), .N(NX), .Output(unary_alu_1_output));
  Unary_ALU unary_alu_2 (.X(Y), .Z(ZY), .N(NY), .Output(unary_alu_2_output));
  assign and_1_out = unary_alu_1_output & unary_alu_2_output;  // AND_Gate and_1, 16 bits wide
  _16_Bit_Adder__2 u_16_bit_adder_2_1 (
    .Sum(n16_bit_adder_2_1_sum), .A(unary_alu_1_output), .B(unary_alu_2_output), .in_1(1'b0));  // open: out_4
  BitSelector #(.width(32), .group(16)) bitselector_1 (
    .in({and_1_out, n16_bit_adder_2_1_sum}), .out(bitselector_1_out), .sel(F));
  assign not_1_out = ~bitselector_1_out;  // NOT_Gate not_1, 16 bits wide
  BitSelector #(.width(32), .group(16)) bitselector_2 (.in({not_1_out, bitselector_1_out}), .out(out_9), .sel(NO));
endmodule
